# Fritzing sketch ESP 01 - programming shield (saved by Fritzing 0.9.3b)
perfboards: 2

parts:
  J2 = male pin header, 8 pins [form="♂ (male)"]
  J3 = male pin header, 2 pins [form="♂ (male)"]
  S1 = Pushbutton [package="[THT]"]
  J5 = double row female pin header, 4 pins [form="♀ (female)"]
  J6 = double row female pin header, 4 pins [form="♀ (female)"]
  J7 = double row female pin header, 4 pins [form="♀ (female)"]  # not connected
  J8 = double row female pin header, 4 pins [form="♀ (female)"]  # not connected
  J9 = double row female pin header, 4 pins [form="♀ (female)"]
  J10 = double row female pin header, 4 pins [form="♀ (female)"]
  J11 = male pin header, 2 pins [form="♂ (male)"]  # not connected
  J12 = male pin header, 8 pins [form="♂ (male)"]
  S2 = Pushbutton [package="[THT]"]
  U5 = ESP8266 ESP-01 Upgraded WiFi Module [part_number=ESP8266]

nets:
  N1: J2.pin3, S1.Pin_1, S1.Pin_2, J6.pin4
  N2: J3.pin1, J6.pin1
  N3: J3.pin2, J5.pin4
  N4: S1.Pin_3, S1.Pin_4, J5.pin2
  N5: J9.pin1, U5.RXD
  N6: J9.pin2, U5.GPIO_0
  N7: J9.pin3, U5.GPIO_2
  N8: J9.pin4, U5.GND
  N9: J10.pin1, U5.VCC
  N10: J10.pin2, U5.RST/GPIO_16
  N11: J10.pin3, U5.CH_PD
  N12: J10.pin4, U5.TXD
  N13: J12.pin3, J12.pin6
  N14: S2.Pin_1, S2.Pin_2
  N15: S2.Pin_3, S2.Pin_4

notes:
  GND
  TX
  3V3
  RST
  EN
  IO0
  IO2
  RX
  Wiring Diagram
  ESP01 Pins
  Shield with plugged ESP01
  VIN
  5V
  3.3V
  RESET
  IOREF
  0>RX
  1<TX

custom parts:
  ESP8266 ESP-01 Upgraded WiFi Module: Upgraded Version ESP-01,all Flash are upgraded to 1M byte.Also support Cloud service remote transmission.
