# Fritzing sketch ESP 01 - using shield (saved by Fritzing 0.9.3b)

parts:
  J1 = female pin header, 6 pins [form="♀ (female)"]  # not connected
  J4 = female pin header, 8 pins [form="♀ (female)"]
  J9 = double row female pin header, 4 pins [form="♀ (female)"]  # not connected
  J10 = double row female pin header, 4 pins [form="♀ (female)"]  # not connected
  J11 = double row female pin header, 4 pins [form="♀ (female)"]
  J12 = double row female pin header, 4 pins [form="♀ (female)"]
  Composant2 = Adafruit Proto Shield for Arduino Kit - v.5
  J2 = female pin header, 6 pins [form="♀ (female)"]  # not connected
  J3 = female pin header, 8 pins [form="♀ (female)"]  # not connected
  Composant3 = Adafruit Proto Shield for Arduino Kit - v.5
  J13 = female pin header, 6 pins [form="♀ (female)"]  # not connected
  J14 = female pin header, 8 pins [form="♀ (female)"]
  J15 = female pin header, 6 pins [form="♀ (female)"]  # not connected
  J16 = female pin header, 8 pins [form="♀ (female)"]  # not connected
  J17 = double row female pin header, 4 pins [form="♀ (female)"]
  J18 = double row female pin header, 4 pins [form="♀ (female)"]
  U12 = ESP8266 ESP-01 Upgraded WiFi Module [part_number=ESP8266]

nets:
  N1: J4.pin1, Composant2.D8
  N2: J4.pin2, Composant2.D9
  N3: J4.pin3, Composant2.D10
  N4: J4.pin4, Composant2.D11
  N5: J4.pin5, Composant2.D12
  N6: J4.pin6, Composant2.D13
  N7: J4.pin7, J12.pin1, Composant2.GND, Composant2.N$84, Composant2.N$113
  N8: J4.pin8, Composant2.AREF
  N9: J11.pin1, Composant2.D4, Composant2.N$37, Composant2.N$217
  N10: J11.pin2, J11.pin4, Composant2.3.3V, Composant2.N$11, Composant2.N$30, Composant2.N$87, Composant2.N$172, Composant2.N$195, Composant2.N$273
  N11: J11.pin3, Composant2.N$196
  N12: J12.pin2, Composant2.N$103
  N13: J12.pin3, Composant2.N$104
  N14: J12.pin4, Composant2.D5, Composant2.N$81, Composant2.N$105
  N15: Composant3.AREF, J14.pin8
  GND: Composant3.GND, Composant3.N$37, J14.pin7, J17.pin1, U12.GND
  N16: Composant3.D13, J14.pin6
  N17: Composant3.D12, J14.pin5
  N18: Composant3.D11, J14.pin4
  N19: Composant3.D10, J14.pin3
  N20: Composant3.D9, J14.pin2
  N21: Composant3.D8, J14.pin1
  N22: Composant3.D4, Composant3.N$217, U12.TXD
  N23: Composant3.D5, Composant3.N$195, J17.pin4, U12.RXD
  3.3V: Composant3.3.3V, Composant3.N$11, Composant3.N$30, Composant3.N$172, Composant3.N$273, U12.VCC, U12.CH_PD
  N24: Composant3.N$87, J17.pin2, U12.GPIO_2
  N25: Composant3.N$103, J18.pin2
  N26: Composant3.N$104, J18.pin3
  N27: Composant3.N$105, J18.pin4
  N28: Composant3.N$113, J18.pin1
  N29: Composant3.N$193, U12.RST/GPIO_16
  N30: Composant3.N$196, J17.pin3, U12.GPIO_0

notes:
  GND
  RX
  IO2
  ESP01 Pins
  EN
  3V3
  TX
  RST
  IO0
  Wiring Diagram
  Digital 5
  Digital 4
  3.3V
  Shield with plugged ESP01

custom parts:
  Adafruit Proto Shield for Arduino Kit - v.5: Arduino prototyping shield designed by Adafruit Industries
  ESP8266 ESP-01 Upgraded WiFi Module: Upgraded Version ESP-01,all Flash are upgraded to 1M byte.Also support Cloud service remote transmission.
