# Fritzing sketch serial communication between arduino and esp (saved by Fritzing 0.9.3b)
breadboards: 1

parts:
  Composant1 = Arduino Uno (Rev3)
  U1 = ESP8266 ESP-01 Upgraded WiFi Module [part_number=ESP8266]
  U2 = POT [package=pot_mammoth]

nets:
  N1: Composant1.A0, U2.A
  N2: Composant1.D4, U1.TXD
  N3: Composant1.D5_PWM, U1.RXD
  3V3: Composant1.3V3, U1.VCC, U1.CH_PD
  N4: Composant1.5V, U2.S
  GND: Composant1.GND, U1.GND, U2.E

custom parts:
  ESP8266 ESP-01 Upgraded WiFi Module: Upgraded Version ESP-01,all Flash are upgraded to 1M byte.Also support Cloud service remote transmission.
