# Fritzing sketch serial communication between arduino and esp (saved by Fritzing 0.9.3b)
breadboards: 1

parts:
  Composant1 = Arduino Uno (Rev3)
  U1 = ESP8266 ESP-01 Upgraded WiFi Module [part_number=ESP8266]
  U2 = POT [package=pot_mammoth]
  U3 = POT [package=pot_mammoth]
  U4 = POT [package=pot_mammoth]
  U5 = POT [package=pot_mammoth]
  U6 = POT [package=pot_mammoth]
  U7 = POT [package=pot_mammoth]

nets:
  N1: Composant1.A0, U2.A
  N2: Composant1.A1, U3.A
  N3: Composant1.A2, U4.A
  N4: Composant1.A3, U5.A
  N5: Composant1.A4/SDA, U6.A
  N6: Composant1.A5/SCL, U7.A
  N7: Composant1.D4, U1.TXD
  N8: Composant1.D5_PWM, U1.RXD
  3V3: Composant1.3V3, U1.VCC, U1.CH_PD
  N9: Composant1.5V, U2.E, U3.E, U4.E, U5.E, U6.E, U7.E
  GND: Composant1.GND, U1.GND, U2.S, U3.S, U4.S, U5.S, U6.S, U7.S

custom parts:
  ESP8266 ESP-01 Upgraded WiFi Module: Upgraded Version ESP-01,all Flash are upgraded to 1M byte.Also support Cloud service remote transmission.
