# Fritzing sketch serial communication between touchboard and esp (saved by Fritzing 0.9.3b)
breadboards: 1

parts:
  U1 = ESP8266 ESP-01 Upgraded WiFi Module [part_number=ESP8266]
  Composant2 = Bare Conductive Touch Board

nets:
  N1: U1.RXD, Composant2.D5/SD-CS_PWM_(SD_Card)
  VCC: U1.VCC, U1.CH_PD, Composant2.3V3
  GND: U1.GND, Composant2.GND
  N2: U1.TXD, Composant2.D4/IRQ_A6_(MPR121)

custom parts:
  ESP8266 ESP-01 Upgraded WiFi Module: Upgraded Version ESP-01,all Flash are upgraded to 1M byte.Also support Cloud service remote transmission.
