# Fritzing sketch esp01-upload-sketch-with-arduino-uno (saved by Fritzing 0.9.3b)
breadboards: 1

parts:
  U1 = ESP8266 ESP-01 Upgraded WiFi Module [part_number=ESP8266]
  U2 = ESP8266 ESP-01 Upgraded WiFi Module [part_number=ESP8266]  # not connected
  Composant1 = Arduino Uno (Rev3)
  S1 = Pushbutton [package="[SMD]"]

nets:
  N1: U1.RXD, Composant1.D0/RX
  GND: U1.GPIO_0, U1.GND, Composant1.RESET, Composant1.GND, S1.Pin_1, S1.Pin_2
  N2: U1.RST/GPIO_16, S1.Pin_3, S1.Pin_4
  N3: U1.CH_PD, Composant1.3V3
  N4: U1.TXD, Composant1.D1/TX

notes:
  TX
  RX
  GND
  3.3V
  RST
  CHPD EN
  GPIO 0
  GPIO 2
  RESET BUTTON

custom parts:
  ESP8266 ESP-01 Upgraded WiFi Module: Upgraded Version ESP-01,all Flash are upgraded to 1M byte.Also support Cloud service remote transmission.
